// Logisim project cpuv2.circ as structural Verilog: 1 circuit, main circuit main
module main (
);

  wire adder_1_cout, ALU_ADD, ALU_CMP, ALU_NAND, ALU_NOR, ALU_SUB, and_1_out, and_2_out, and_3_out,
       and_4_out, and_5_out, and_6_out, and_8_out, and_10_out, and_11_out, and_12_out, and_13_out,
       and_14_out, and_15_out, and_16_out, and_17_out, and_18_out, and_19_out, and_20_out, and_21_out,
       and_22_out, and_23_out, and_24_out, and_25_out, and_26_out, and_27_out, and_28_out, and_29_out,
       and_30_out, and_31_out, and_32_out, and_33_out, and_34_out, and_35_out, and_36_out, and_37_out,
       and_38_out, and_39_out, and_40_out, and_41_out, and_42_out, and_43_out, and_44_out, and_45_out,
       and_46_out, and_47_out, and_48_out, and_49_out, and_50_out, and_51_out, and_52_out, and_53_out,
       and_54_out, and_55_out, and_56_out, and_57_out, and_58_out, and_59_out, and_60_out, and_61_out,
       and_62_out, and_63_out, and_64_out, and_65_out, and_66_out, and_67_out, and_68_out, and_69_out,
       and_70_out, and_71_out, and_72_out, and_73_out, and_74_out, and_75_out, and_76_out, and_77_out,
       button_2_out, clk, clock_1_out, COND_INVERT, counter_1_carry, d_ff_1_q, d_ff_2_q, d_ff_3_q, d_ff_4_q,
       d_ff_5_q, d_ff_6_q, halt, IO_IN, IO_OUT, memory_read, memory_write, nand_1_out, nand_2_out,
       nand_3_out, nand_4_out, nand_5_out, nand_6_out, nand_7_out, nand_8_out, nor_1_out, nor_2_out,
       nor_3_out, nor_4_out, nor_5_out, nor_6_out, nor_7_out, nor_8_out, not_1_out, not_2_out, not_3_out,
       not_4_out, not_5_out, not_6_out, not_7_out, not_8_out, not_9_out, not_10_out, not_11_out, not_12_out,
       not_13_out, not_14_out, not_15_out, not_16_out, not_17_out, not_18_out, not_19_out, not_20_out,
       not_21_out, not_22_out, not_23_out, not_24_out, not_25_out, not_26_out, not_27_out, not_28_out,
       not_29_out, not_30_out, not_31_out, not_32_out, not_33_out, not_34_out, not_35_out, not_36_out,
       not_37_out, not_38_out, not_39_out, not_40_out, not_41_out, not_42_out, not_43_out, not_44_out,
       not_45_out, not_46_out, not_47_out, not_48_out, not_49_out, not_50_out, not_51_out, not_52_out,
       not_53_out, not_54_out, not_55_out, not_56_out, not_57_out, not_58_out, not_59_out, not_60_out,
       or_1_out, or_2_out, or_3_out, or_4_out, or_5_out, or_6_out, or_7_out, or_8_out, or_9_out, or_10_out,
       or_11_out, or_12_out, or_15_out, or_16_out, or_17_out, or_18_out, or_19_out, or_20_out, or_23_out,
       or_24_out, or_25_out, or_26_out, pc_count, PC_FLUSH, PC_FLUSH_COND, pc_load, pc_out_address_bus,
       pull_resistor_1_node, pull_resistor_27_node, pull_resistor_69_node, PUT_A_ADDR, PUT_ALUOUT_DB,
       PUT_B_ADDR, PUT_IADR_ADDR, PUT_IIMM_DB, PUT_IR0_DB, PUT_IR1_DB, reset, SAVE_ADDR_A, SAVE_ADDR_B,
       SAVE_DB_ALUA, SAVE_DB_ALUB, SAVE_DB_IR0, SAVE_DB_IR1, SAVE_PCB, SAVE_PCB_IF_EQ, SAVE_PCB_IF_Z,
       subtractor_1_bout, transistor_41_out, transistor_42_out, transistor_43_out, transistor_44_out,
       transistor_45_out, transistor_46_out, transistor_47_out, transistor_48_out, transistor_49_out,
       transistor_50_out, transistor_51_out, transistor_52_out, transistor_53_out, transistor_54_out,
       transistor_55_out, transistor_88_out, transistor_145_out, transistor_146_out, transistor_147_out,
       transistor_148_out, transistor_149_out, transistor_150_out, transistor_151_out, transistor_152_out,
       transistor_177_out, transistor_178_out, transistor_179_out, transistor_180_out, transistor_181_out,
       transistor_182_out, transistor_183_out, transistor_184_out, xnor_1_out, xnor_2_out, xnor_3_out,
       xnor_4_out, xnor_5_out, xnor_6_out, xnor_7_out, xnor_8_out, xnor_9_out, xnor_10_out, xnor_11_out,
       xnor_12_out, xnor_13_out, xnor_14_out, xnor_15_out, xnor_16_out, xor_1_out, xor_2_out, xor_3_out,
       xor_4_out, xor_5_out, xor_6_out, xor_7_out, xor_8_out, xor_9_out, xor_10_out, xor_11_out, xor_12_out,
       xor_13_out;
  wire [2:0] counter_1_q;
  wire [3:0] fg, instruction_reg0, instruction_reg1;
  wire [7:0] adder_1_out, data_bus, or_13_out, or_14_out, or_21_out, or_22_out, pull_resistor_28_node,
       pull_resistor_78_node, pull_resistor_86_node, pull_resistor_96_node, pull_resistor_104_node,
       ram_1_dout, register_2_q, register_4_q, register_5_q, register_6_q, register_7_q, register_8_q,
       register_9_q, register_10_q, register_11_q, register_12_q, register_13_q, register_14_q, rom_1_data,
       subtractor_1_out, transistor_113_out;
  wire [15:0] address_bus, counter_2_q, register_1_q;
  wire [31:0] rom_2_data;

  Pull_Resistor pull_resistor_1 (.node(pull_resistor_1_node));
  // Switch switch_1: pin names not known; wires that end beside it: 1'b1, pull_resistor_1_node, reset
  Pull_Resistor pull_resistor_2 (.node(address_bus[0]));
  Pull_Resistor pull_resistor_3 (.node(address_bus[1]));
  Pull_Resistor pull_resistor_4 (.node(address_bus[2]));
  Pull_Resistor pull_resistor_5 (.node(address_bus[3]));
  Pull_Resistor pull_resistor_6 (.node(address_bus[4]));
  Pull_Resistor pull_resistor_7 (.node(address_bus[5]));
  Pull_Resistor pull_resistor_8 (.node(address_bus[6]));
  Pull_Resistor pull_resistor_9 (.node(address_bus[7]));
  Pull_Resistor pull_resistor_10 (.node(address_bus[8]));
  Pull_Resistor pull_resistor_11 (.node(address_bus[9]));
  Pull_Resistor pull_resistor_12 (.node(address_bus[10]));
  Pull_Resistor pull_resistor_13 (.node(address_bus[11]));
  Pull_Resistor pull_resistor_14 (.node(address_bus[12]));
  Pull_Resistor pull_resistor_15 (.node(address_bus[13]));
  Pull_Resistor pull_resistor_16 (.node(address_bus[14]));
  Pull_Resistor pull_resistor_17 (.node(address_bus[15]));
  Pull_Resistor pull_resistor_18 (.node(data_bus[0]));
  Pull_Resistor pull_resistor_19 (.node(data_bus[1]));
  Pull_Resistor pull_resistor_20 (.node(data_bus[2]));
  Pull_Resistor pull_resistor_21 (.node(data_bus[3]));
  Pull_Resistor pull_resistor_22 (.node(data_bus[4]));
  Pull_Resistor pull_resistor_23 (.node(data_bus[5]));
  Pull_Resistor pull_resistor_24 (.node(data_bus[6]));
  Pull_Resistor pull_resistor_25 (.node(data_bus[7]));
  Button button_1 (.out(reset));
  Button button_2 (.out(button_2_out));
  Clock clock_1 (.out(clock_1_out));
  and and_1 (and_1_out, clock_1_out, pull_resistor_1_node);
  or or_1 (or_1_out, d_ff_5_q, reset);
  not not_1 (not_1_out, d_ff_4_q);
  ROM #(.addrWidth(15)) rom_1 (.addr(address_bus[14:0]), .data(rom_1_data));
  RAM #(.addrWidth(15), .enables("line"), .trigger("falling")) ram_1 (
    .addr(address_bus[14:0]), .we(and_6_out), .clk(and_8_out), .din(data_bus), .dout(ram_1_dout));
  or or_2 (or_2_out, PC_FLUSH, pc_count);
  Register #(.trigger("falling"), .width(16)) register_1 (
    .D(address_bus), .en(SAVE_PCB), .clk(clk), .Q(register_1_q), .clr(reset));
  and and_2 (and_2_out, clk, or_3_out);
  not not_2 (not_2_out, d_ff_4_q);
  or or_3 (or_3_out, not_2_out, or_6_out);
  Counter #(.max('h7), .width(3)) counter_1 (
    .clr(xor_3_out), .up(1'b1), .clk(and_3_out), .carry(counter_1_carry), .Q(counter_1_q));  // open: load, count, D
  and and_3 (and_3_out, clk, d_ff_4_q);
  Counter #(.max('hffff), .width(16)) counter_2 (
    .clr(reset), .load(PC_FLUSH), .up(1'b1), .clk(or_2_out), .D(register_1_q), .carry(halt), .Q(counter_2_q));  // open: count
  or or_4 (or_4_out, button_2_out, and_1_out);
  D_Flip_Flop d_ff_1 (.D(1'b1), .clk(and_2_out), .Q(d_ff_1_q), .reset(or_1_out));  // open: Qn, preset
  or or_5 (or_5_out, or_1_out, reset);
  or or_6 (or_6_out, transistor_88_out, counter_1_carry);
  not not_3 (not_3_out, address_bus[15]);
  not not_4 (not_4_out, fg[3]);
  D_Flip_Flop d_ff_2 (.D(d_ff_1_q), .clk(and_2_out), .Q(d_ff_2_q), .reset(or_1_out));  // open: Qn, preset
  xor xor_1 (xor_1_out, d_ff_1_q, d_ff_2_q);
  Register #(.trigger("falling")) register_2 (
    .D(data_bus), .en(xor_1_out), .clk(clk), .Q(register_2_q), .clr(or_5_out));
  and and_4 (and_4_out, not_3_out, memory_read);
  and and_5 (and_5_out, address_bus[15], memory_read);
  and and_6 (and_6_out, address_bus[15], memory_write);
  and and_7 (clk, or_4_out, not_4_out);
  D_Flip_Flop d_ff_3 (.D(d_ff_2_q), .clk(and_2_out), .Q(d_ff_3_q), .reset(or_1_out));  // open: Qn, preset
  xor xor_2 (xor_2_out, d_ff_2_q, d_ff_3_q);
  Register #(.trigger("falling")) register_3 (
    .D(data_bus), .en(xor_2_out), .clk(clk), .Q({instruction_reg1, instruction_reg0}), .clr(or_5_out));
  not not_5 (not_5_out, PUT_IIMM_DB);
  not not_6 (not_6_out, and_4_out);
  not not_7 (not_7_out, and_5_out);
  and and_8 (and_8_out, and_6_out, clk);
  not not_8 (not_8_out, pc_out_address_bus);
  D_Flip_Flop d_ff_4 (.D(d_ff_3_q), .clk(and_2_out), .Q(d_ff_4_q), .reset(or_1_out));  // open: Qn, preset
  xor xor_3 (xor_3_out, d_ff_3_q, d_ff_4_q);
  Register #(.trigger("falling")) register_4 (
    .D(data_bus), .en(xor_3_out), .clk(clk), .Q(register_4_q), .clr(or_5_out));
  Transistor transistor_1 (.in(register_4_q[0]), .out(data_bus[0]), .gate(not_5_out));
  Transistor transistor_2 (.in(register_4_q[1]), .out(data_bus[1]), .gate(not_5_out));
  Transistor transistor_3 (.in(register_4_q[2]), .out(data_bus[2]), .gate(not_5_out));
  Transistor transistor_4 (.in(register_4_q[3]), .out(data_bus[3]), .gate(not_5_out));
  Transistor transistor_5 (.in(register_4_q[4]), .out(data_bus[4]), .gate(not_5_out));
  Transistor transistor_6 (.in(register_4_q[5]), .out(data_bus[5]), .gate(not_5_out));
  Transistor transistor_7 (.in(register_4_q[6]), .out(data_bus[6]), .gate(not_5_out));
  Transistor transistor_8 (.in(register_4_q[7]), .out(data_bus[7]), .gate(not_5_out));
  Transistor transistor_9 (.in(rom_1_data[0]), .out(data_bus[0]), .gate(not_6_out));
  Transistor transistor_10 (.in(rom_1_data[1]), .out(data_bus[1]), .gate(not_6_out));
  Transistor transistor_11 (.in(rom_1_data[2]), .out(data_bus[2]), .gate(not_6_out));
  Transistor transistor_12 (.in(rom_1_data[3]), .out(data_bus[3]), .gate(not_6_out));
  Transistor transistor_13 (.in(rom_1_data[4]), .out(data_bus[4]), .gate(not_6_out));
  Transistor transistor_14 (.in(rom_1_data[5]), .out(data_bus[5]), .gate(not_6_out));
  Transistor transistor_15 (.in(rom_1_data[6]), .out(data_bus[6]), .gate(not_6_out));
  Transistor transistor_16 (.in(rom_1_data[7]), .out(data_bus[7]), .gate(not_6_out));
  Transistor transistor_17 (.in(ram_1_dout[0]), .out(data_bus[0]), .gate(not_7_out));
  Transistor transistor_18 (.in(ram_1_dout[1]), .out(data_bus[1]), .gate(not_7_out));
  Transistor transistor_19 (.in(ram_1_dout[2]), .out(data_bus[2]), .gate(not_7_out));
  Transistor transistor_20 (.in(ram_1_dout[3]), .out(data_bus[3]), .gate(not_7_out));
  Transistor transistor_21 (.in(ram_1_dout[4]), .out(data_bus[4]), .gate(not_7_out));
  Transistor transistor_22 (.in(ram_1_dout[5]), .out(data_bus[5]), .gate(not_7_out));
  Transistor transistor_23 (.in(ram_1_dout[6]), .out(data_bus[6]), .gate(not_7_out));
  Transistor transistor_24 (.in(ram_1_dout[7]), .out(data_bus[7]), .gate(not_7_out));
  D_Flip_Flop d_ff_5 (.D(d_ff_4_q), .clk(and_2_out), .Q(d_ff_5_q), .reset(or_1_out));  // open: Qn, preset
  ROM #(.addrWidth(11), .dataWidth(32)) rom_2 (.addr({register_2_q, counter_1_q}), .data(rom_2_data));
  Transistor transistor_25 (.in(counter_2_q[0]), .out(address_bus[0]), .gate(not_8_out));
  Transistor transistor_26 (.in(counter_2_q[1]), .out(address_bus[1]), .gate(not_8_out));
  Transistor transistor_27 (.in(counter_2_q[2]), .out(address_bus[2]), .gate(not_8_out));
  Transistor transistor_28 (.in(counter_2_q[3]), .out(address_bus[3]), .gate(not_8_out));
  Transistor transistor_29 (.in(counter_2_q[4]), .out(address_bus[4]), .gate(not_8_out));
  Transistor transistor_30 (.in(counter_2_q[5]), .out(address_bus[5]), .gate(not_8_out));
  Transistor transistor_31 (.in(counter_2_q[6]), .out(address_bus[6]), .gate(not_8_out));
  Transistor transistor_32 (.in(counter_2_q[7]), .out(address_bus[7]), .gate(not_8_out));
  Transistor transistor_33 (.in(counter_2_q[8]), .out(address_bus[8]), .gate(not_8_out));
  Transistor transistor_34 (.in(counter_2_q[9]), .out(address_bus[9]), .gate(not_8_out));
  Transistor transistor_35 (.in(counter_2_q[10]), .out(address_bus[10]), .gate(not_8_out));
  Transistor transistor_36 (.in(counter_2_q[11]), .out(address_bus[11]), .gate(not_8_out));
  Transistor transistor_37 (.in(counter_2_q[12]), .out(address_bus[12]), .gate(not_8_out));
  Transistor transistor_38 (.in(counter_2_q[13]), .out(address_bus[13]), .gate(not_8_out));
  Transistor transistor_39 (.in(counter_2_q[14]), .out(address_bus[14]), .gate(not_8_out));
  Transistor transistor_40 (.in(counter_2_q[15]), .out(address_bus[15]), .gate(not_8_out));
  Pull_Resistor pull_resistor_26 (.node(or_1_out));
  not not_9 (not_9_out, and_2_out);
  and and_9 (pc_count, not_9_out, or_7_out);
  or or_7 (or_7_out, xor_3_out, xor_2_out, xor_1_out);
  buf buffer_1 (pc_out_address_bus, or_7_out);
  buf buffer_2 (memory_read, or_7_out);
  xnor xnor_1 (xnor_1_out, address_bus[0], 1'b1);
  Transistor transistor_41 (.in(1'b1), .out(transistor_41_out), .gate(xnor_1_out));
  xnor xnor_2 (xnor_2_out, address_bus[1], 1'b1);
  Transistor transistor_42 (.in(transistor_41_out), .out(transistor_42_out), .gate(xnor_2_out));
  xnor xnor_3 (xnor_3_out, address_bus[2], 1'b1);
  Transistor transistor_43 (.in(transistor_42_out), .out(transistor_43_out), .gate(xnor_3_out));
  xnor xnor_4 (xnor_4_out, address_bus[3], 1'b1);
  Transistor transistor_44 (.in(transistor_43_out), .out(transistor_44_out), .gate(xnor_4_out));
  xnor xnor_5 (xnor_5_out, address_bus[4], 1'b1);
  Transistor transistor_45 (.in(transistor_44_out), .out(transistor_45_out), .gate(xnor_5_out));
  xnor xnor_6 (xnor_6_out, address_bus[5], 1'b1);
  Transistor transistor_46 (.in(transistor_45_out), .out(transistor_46_out), .gate(xnor_6_out));
  xnor xnor_7 (xnor_7_out, address_bus[6], 1'b1);
  Transistor transistor_47 (.in(transistor_46_out), .out(transistor_47_out), .gate(xnor_7_out));
  xnor xnor_8 (xnor_8_out, address_bus[7], 1'b1);
  Transistor transistor_48 (.in(transistor_47_out), .out(transistor_48_out), .gate(xnor_8_out));
  xnor xnor_9 (xnor_9_out, address_bus[8], 1'b1);
  Transistor transistor_49 (.in(transistor_48_out), .out(transistor_49_out), .gate(xnor_9_out));
  xnor xnor_10 (xnor_10_out, address_bus[9], 1'b1);
  Transistor transistor_50 (.in(transistor_49_out), .out(transistor_50_out), .gate(xnor_10_out));
  xnor xnor_11 (xnor_11_out, address_bus[10], 1'b1);
  Transistor transistor_51 (.in(transistor_50_out), .out(transistor_51_out), .gate(xnor_11_out));
  xnor xnor_12 (xnor_12_out, address_bus[11], 1'b1);
  Transistor transistor_52 (.in(transistor_51_out), .out(transistor_52_out), .gate(xnor_12_out));
  xnor xnor_13 (xnor_13_out, address_bus[12], 1'b1);
  Transistor transistor_53 (.in(transistor_52_out), .out(transistor_53_out), .gate(xnor_13_out));
  xnor xnor_14 (xnor_14_out, address_bus[13], 1'b1);
  Transistor transistor_54 (.in(transistor_53_out), .out(transistor_54_out), .gate(xnor_14_out));
  xnor xnor_15 (xnor_15_out, address_bus[14], 1'b1);
  Transistor transistor_55 (.in(transistor_54_out), .out(transistor_55_out), .gate(xnor_15_out));
  xnor xnor_16 (xnor_16_out, address_bus[15], 1'b1);
  Pull_Resistor pull_resistor_27 (.node(pull_resistor_27_node));
  Transistor transistor_56 (.in(transistor_55_out), .out(pull_resistor_27_node), .gate(xnor_16_out));
  Pull_Resistor pull_resistor_28 (.node(pull_resistor_28_node[0]));
  Pull_Resistor pull_resistor_29 (.node(pull_resistor_28_node[1]));
  Pull_Resistor pull_resistor_30 (.node(pull_resistor_28_node[2]));
  Pull_Resistor pull_resistor_31 (.node(pull_resistor_28_node[3]));
  Pull_Resistor pull_resistor_32 (.node(pull_resistor_28_node[4]));
  Pull_Resistor pull_resistor_33 (.node(pull_resistor_28_node[5]));
  Pull_Resistor pull_resistor_34 (.node(pull_resistor_28_node[6]));
  Pull_Resistor pull_resistor_35 (.node(pull_resistor_28_node[7]));
  Pull_Resistor pull_resistor_36 (.node(memory_read));
  Pull_Resistor pull_resistor_37 (.node(memory_write));
  Transistor transistor_57 (.in(rom_2_data[0]), .out(PUT_A_ADDR), .gate(not_1_out));
  Transistor transistor_58 (.in(rom_2_data[1]), .out(PUT_IR0_DB), .gate(not_1_out));
  Transistor transistor_59 (.in(rom_2_data[2]), .out(PUT_IR1_DB), .gate(not_1_out));
  Transistor transistor_60 (.in(rom_2_data[3]), .out(SAVE_DB_IR0), .gate(not_1_out));
  Transistor transistor_61 (.in(rom_2_data[4]), .out(SAVE_DB_IR1), .gate(not_1_out));
  Transistor transistor_62 (.in(rom_2_data[5]), .out(PUT_IIMM_DB), .gate(not_1_out));
  Transistor transistor_63 (.in(rom_2_data[6]), .out(SAVE_DB_ALUA), .gate(not_1_out));
  Transistor transistor_64 (.in(rom_2_data[7]), .out(SAVE_DB_ALUB), .gate(not_1_out));
  Transistor transistor_65 (.in(rom_2_data[8]), .out(ALU_ADD), .gate(not_1_out));
  Transistor transistor_66 (.in(rom_2_data[9]), .out(ALU_CMP), .gate(not_1_out));
  Transistor transistor_67 (.in(rom_2_data[10]), .out(PUT_ALUOUT_DB), .gate(not_1_out));
  Transistor transistor_68 (.in(rom_2_data[11]), .out(COND_INVERT), .gate(not_1_out));
  Transistor transistor_69 (.in(rom_2_data[12]), .out(SAVE_PCB_IF_Z), .gate(not_1_out));
  Transistor transistor_70 (.in(rom_2_data[13]), .out(SAVE_PCB_IF_EQ), .gate(not_1_out));
  Transistor transistor_71 (.in(rom_2_data[14]), .out(SAVE_PCB), .gate(not_1_out));
  Transistor transistor_72 (.in(rom_2_data[15]), .out(memory_write), .gate(not_1_out));
  Transistor transistor_73 (.in(rom_2_data[16]), .out(memory_read), .gate(not_1_out));
  Transistor transistor_74 (.in(rom_2_data[17]), .out(PC_FLUSH), .gate(not_1_out));
  Transistor transistor_75 (.in(rom_2_data[18]), .out(PC_FLUSH_COND), .gate(not_1_out));
  Transistor transistor_76 (.in(rom_2_data[19]), .out(ALU_SUB), .gate(not_1_out));
  Transistor transistor_77 (.in(rom_2_data[20]), .out(ALU_NAND), .gate(not_1_out));
  Transistor transistor_78 (.in(rom_2_data[21]), .out(ALU_NOR), .gate(not_1_out));
  Transistor transistor_79 (.in(rom_2_data[22]), .out(IO_IN), .gate(not_1_out));
  Transistor transistor_80 (.in(rom_2_data[23]), .out(IO_OUT), .gate(not_1_out));
  Transistor transistor_81 (.in(rom_2_data[24]), .out(PUT_B_ADDR), .gate(not_1_out));
  Transistor transistor_82 (.in(rom_2_data[25]), .out(PUT_IADR_ADDR), .gate(not_1_out));
  Transistor transistor_83 (.in(rom_2_data[26]), .out(SAVE_ADDR_A), .gate(not_1_out));
  Transistor transistor_84 (.in(rom_2_data[27]), .out(SAVE_ADDR_B), .gate(not_1_out));
  Transistor transistor_85 (.in(rom_2_data[28]), .gate(not_1_out));  // open: out
  Transistor transistor_86 (.in(rom_2_data[29]), .gate(not_1_out));  // open: out
  Transistor transistor_87 (.in(rom_2_data[30]), .gate(not_1_out));  // open: out
  Transistor transistor_88 (.in(rom_2_data[31]), .out(transistor_88_out), .gate(not_1_out));
  and and_10 (and_10_out, pull_resistor_27_node, IO_OUT);
  buf and_11 (and_11_out, pull_resistor_27_node);  // AND_Gate
  not not_10 (not_10_out, and_11_out);
  Transistor transistor_89 (.in(pull_resistor_28_node[0]), .out(data_bus[0]), .gate(not_10_out));
  Transistor transistor_90 (.in(pull_resistor_28_node[1]), .out(data_bus[1]), .gate(not_10_out));
  Transistor transistor_91 (.in(pull_resistor_28_node[2]), .out(data_bus[2]), .gate(not_10_out));
  Transistor transistor_92 (.in(pull_resistor_28_node[3]), .out(data_bus[3]), .gate(not_10_out));
  Transistor transistor_93 (.in(pull_resistor_28_node[4]), .out(data_bus[4]), .gate(not_10_out));
  Transistor transistor_94 (.in(pull_resistor_28_node[5]), .out(data_bus[5]), .gate(not_10_out));
  Transistor transistor_95 (.in(pull_resistor_28_node[6]), .out(data_bus[6]), .gate(not_10_out));
  Transistor transistor_96 (.in(pull_resistor_28_node[7]), .out(data_bus[7]), .gate(not_10_out));
  Pull_Resistor pull_resistor_38 (.node(transistor_88_out));
  Register #(.trigger("falling")) register_5 (.D(data_bus), .en(and_10_out), .clk(clk), .Q(register_5_q), .clr(reset));
  Pull_Resistor pull_resistor_39 (.node(pc_load));
  Pull_Resistor pull_resistor_40 (.node(pc_out_address_bus));
  Pull_Resistor pull_resistor_41 (.node(PUT_A_ADDR));
  Pull_Resistor pull_resistor_42 (.node(PUT_IR0_DB));
  Pull_Resistor pull_resistor_43 (.node(PUT_IR1_DB));
  Pull_Resistor pull_resistor_44 (.node(SAVE_DB_IR0));
  Pull_Resistor pull_resistor_45 (.node(SAVE_DB_IR1));
  Pull_Resistor pull_resistor_46 (.node(PUT_IIMM_DB));
  Pull_Resistor pull_resistor_47 (.node(SAVE_DB_ALUA));
  Pull_Resistor pull_resistor_48 (.node(SAVE_DB_ALUB));
  Pull_Resistor pull_resistor_49 (.node(ALU_ADD));
  Pull_Resistor pull_resistor_50 (.node(ALU_CMP));
  Pull_Resistor pull_resistor_51 (.node(PUT_ALUOUT_DB));
  Pull_Resistor pull_resistor_52 (.node(COND_INVERT));
  Pull_Resistor pull_resistor_53 (.node(SAVE_PCB_IF_Z));
  Pull_Resistor pull_resistor_54 (.node(SAVE_PCB_IF_EQ));
  Pull_Resistor pull_resistor_55 (.node(SAVE_PCB));
  Pull_Resistor pull_resistor_56 (.node(memory_write));
  Pull_Resistor pull_resistor_57 (.node(memory_read));
  Pull_Resistor pull_resistor_58 (.node(PC_FLUSH));
  Pull_Resistor pull_resistor_59 (.node(PC_FLUSH_COND));
  Pull_Resistor pull_resistor_60 (.node(ALU_SUB));
  Pull_Resistor pull_resistor_61 (.node(ALU_NAND));
  Pull_Resistor pull_resistor_62 (.node(ALU_NOR));
  Pull_Resistor pull_resistor_63 (.node(IO_IN));
  Pull_Resistor pull_resistor_64 (.node(IO_OUT));
  Pull_Resistor pull_resistor_65 (.node(PUT_B_ADDR));
  Pull_Resistor pull_resistor_66 (.node(PUT_IADR_ADDR));
  Pull_Resistor pull_resistor_67 (.node(SAVE_ADDR_A));
  Pull_Resistor pull_resistor_68 (.node(SAVE_ADDR_B));
  Transistor transistor_97 (.in(instruction_reg0[0]), .out(address_bus[0]), .gate(not_11_out));
  Transistor transistor_98 (.in(instruction_reg0[1]), .out(address_bus[1]), .gate(not_11_out));
  Transistor transistor_99 (.in(instruction_reg0[2]), .out(address_bus[2]), .gate(not_11_out));
  Transistor transistor_100 (.in(instruction_reg0[3]), .out(address_bus[3]), .gate(not_11_out));
  Transistor transistor_101 (.in(instruction_reg1[0]), .out(address_bus[4]), .gate(not_11_out));
  Transistor transistor_102 (.in(instruction_reg1[1]), .out(address_bus[5]), .gate(not_11_out));
  Transistor transistor_103 (.in(instruction_reg1[2]), .out(address_bus[6]), .gate(not_11_out));
  Transistor transistor_104 (.in(instruction_reg1[3]), .out(address_bus[7]), .gate(not_11_out));
  Transistor transistor_105 (.in(register_4_q[0]), .out(address_bus[8]), .gate(not_11_out));
  Transistor transistor_106 (.in(register_4_q[1]), .out(address_bus[9]), .gate(not_11_out));
  Transistor transistor_107 (.in(register_4_q[2]), .out(address_bus[10]), .gate(not_11_out));
  Transistor transistor_108 (.in(register_4_q[3]), .out(address_bus[11]), .gate(not_11_out));
  Transistor transistor_109 (.in(register_4_q[4]), .out(address_bus[12]), .gate(not_11_out));
  Transistor transistor_110 (.in(register_4_q[5]), .out(address_bus[13]), .gate(not_11_out));
  Transistor transistor_111 (.in(register_4_q[6]), .out(address_bus[14]), .gate(not_11_out));
  Transistor transistor_112 (.in(register_4_q[7]), .out(address_bus[15]), .gate(not_11_out));
  not not_11 (not_11_out, PUT_IADR_ADDR);
  xor xor_4 (xor_4_out, COND_INVERT, fg[0]);
  and and_12 (and_12_out, xor_4_out, SAVE_PCB_IF_Z);
  xor xor_5 (xor_5_out, COND_INVERT, fg[1]);
  and and_13 (and_13_out, xor_5_out, SAVE_PCB_IF_EQ);
  buf buffer_3 (SAVE_PCB, and_12_out);
  buf buffer_4 (SAVE_PCB, and_13_out);
  or or_8 (or_8_out, SAVE_PCB_IF_Z, SAVE_PCB_IF_EQ);
  or or_9 (or_9_out, and_12_out, and_13_out);
  D_Flip_Flop d_ff_6 (.clk(clk), .Q(d_ff_6_q), .preset(or_9_out), .reset(or_8_out));  // open: D, Qn
  Register #(.trigger("falling")) register_6 (
    .D(data_bus), .en(SAVE_DB_ALUA), .clk(clk), .Q(register_6_q), .clr(reset));
  Register #(.trigger("falling")) register_7 (
    .D(data_bus), .en(SAVE_DB_ALUB), .clk(clk), .Q(register_7_q), .clr(reset));
  and and_14 (and_14_out, d_ff_6_q, PC_FLUSH_COND);
  buf buffer_5 (PC_FLUSH, and_14_out);
  D_Flip_Flop #(.trigger("falling")) d_ff_7 (
    .D(1'b0), .clk(and_15_out), .Q(fg[3]), .preset(halt), .reset(reset));  // open: Qn
  and and_15 (and_15_out, ALU_CMP, clk);
  nand nand_1 (nand_1_out, register_7_q[0], register_6_q[0]);
  nand nand_2 (nand_2_out, register_7_q[1], register_6_q[1]);
  nand nand_3 (nand_3_out, register_7_q[2], register_6_q[2]);
  nand nand_4 (nand_4_out, register_7_q[3], register_6_q[3]);
  nand nand_5 (nand_5_out, register_7_q[4], register_6_q[4]);
  nand nand_6 (nand_6_out, register_7_q[5], register_6_q[5]);
  nand nand_7 (nand_7_out, register_7_q[6], register_6_q[6]);
  nand nand_8 (nand_8_out, register_7_q[7], register_6_q[7]);
  not not_12 (not_12_out, ALU_NAND);
  Adder adder_1 (.a(register_6_q), .b(register_7_q), .out(adder_1_out), .cout(adder_1_cout));  // open: cin
  and and_16 (and_16_out, adder_1_cout, ALU_ADD);
  Subtractor subtractor_1 (
    .a(register_6_q), .b(register_7_q), .out(subtractor_1_out), .bout(subtractor_1_bout));  // open: bin
  and and_17 (and_17_out, subtractor_1_bout, ALU_SUB);
  Transistor transistor_113 (.in(nand_1_out), .out(transistor_113_out[0]), .gate(not_12_out));
  Transistor transistor_114 (.in(nand_2_out), .out(transistor_113_out[1]), .gate(not_12_out));
  Transistor transistor_115 (.in(nand_3_out), .out(transistor_113_out[2]), .gate(not_12_out));
  Transistor transistor_116 (.in(nand_4_out), .out(transistor_113_out[3]), .gate(not_12_out));
  Transistor transistor_117 (.in(nand_5_out), .out(transistor_113_out[4]), .gate(not_12_out));
  Transistor transistor_118 (.in(nand_6_out), .out(transistor_113_out[5]), .gate(not_12_out));
  Transistor transistor_119 (.in(nand_7_out), .out(transistor_113_out[6]), .gate(not_12_out));
  Transistor transistor_120 (.in(nand_8_out), .out(transistor_113_out[7]), .gate(not_12_out));
  not not_13 (not_13_out, ALU_ADD);
  Pull_Resistor pull_resistor_69 (.node(pull_resistor_69_node));
  buf buffer_6 (pull_resistor_69_node, and_16_out);
  not not_14 (not_14_out, ALU_SUB);
  buf buffer_7 (pull_resistor_69_node, and_17_out);
  D_Flip_Flop #(.trigger("falling")) d_ff_8 (
    .D(1'b0), .clk(and_15_out), .Q(fg[2]), .preset(pull_resistor_69_node), .reset(reset));  // open: Qn
  not not_15 (not_15_out, instruction_reg0[0]);
  not not_16 (not_16_out, instruction_reg0[1]);
  not not_17 (not_17_out, instruction_reg0[2]);
  not not_18 (not_18_out, instruction_reg0[3]);
  not not_19 (not_19_out, instruction_reg1[0]);
  not not_20 (not_20_out, instruction_reg1[1]);
  not not_21 (not_21_out, instruction_reg1[2]);
  not not_22 (not_22_out, instruction_reg1[3]);
  not not_23 (not_23_out, instruction_reg0[1]);
  not not_24 (not_24_out, instruction_reg0[2]);
  not not_25 (not_25_out, instruction_reg0[3]);
  not not_26 (not_26_out, instruction_reg1[1]);
  not not_27 (not_27_out, instruction_reg1[2]);
  not not_28 (not_28_out, instruction_reg1[3]);
  Transistor transistor_121 (.in(adder_1_out[0]), .out(transistor_113_out[0]), .gate(not_13_out));
  Transistor transistor_122 (.in(adder_1_out[1]), .out(transistor_113_out[1]), .gate(not_13_out));
  Transistor transistor_123 (.in(adder_1_out[2]), .out(transistor_113_out[2]), .gate(not_13_out));
  Transistor transistor_124 (.in(adder_1_out[3]), .out(transistor_113_out[3]), .gate(not_13_out));
  Transistor transistor_125 (.in(adder_1_out[4]), .out(transistor_113_out[4]), .gate(not_13_out));
  Transistor transistor_126 (.in(adder_1_out[5]), .out(transistor_113_out[5]), .gate(not_13_out));
  Transistor transistor_127 (.in(adder_1_out[6]), .out(transistor_113_out[6]), .gate(not_13_out));
  Transistor transistor_128 (.in(adder_1_out[7]), .out(transistor_113_out[7]), .gate(not_13_out));
  Transistor transistor_129 (.in(subtractor_1_out[0]), .out(transistor_113_out[0]), .gate(not_14_out));
  Transistor transistor_130 (.in(subtractor_1_out[1]), .out(transistor_113_out[1]), .gate(not_14_out));
  Transistor transistor_131 (.in(subtractor_1_out[2]), .out(transistor_113_out[2]), .gate(not_14_out));
  Transistor transistor_132 (.in(subtractor_1_out[3]), .out(transistor_113_out[3]), .gate(not_14_out));
  Transistor transistor_133 (.in(subtractor_1_out[4]), .out(transistor_113_out[4]), .gate(not_14_out));
  Transistor transistor_134 (.in(subtractor_1_out[5]), .out(transistor_113_out[5]), .gate(not_14_out));
  Transistor transistor_135 (.in(subtractor_1_out[6]), .out(transistor_113_out[6]), .gate(not_14_out));
  Transistor transistor_136 (.in(subtractor_1_out[7]), .out(transistor_113_out[7]), .gate(not_14_out));
  D_Flip_Flop #(.trigger("falling")) d_ff_9 (
    .D(transistor_184_out), .clk(and_15_out), .Q(fg[1]), .reset(reset));  // open: Qn, preset
  and and_18 (and_18_out, not_15_out, not_16_out);
  and and_19 (and_19_out, not_17_out, not_18_out);
  and and_20 (and_20_out, not_19_out, not_20_out);
  and and_21 (and_21_out, not_21_out, not_22_out);
  and and_22 (and_22_out, instruction_reg0[0], not_23_out);
  and and_23 (and_23_out, not_24_out, not_25_out);
  and and_24 (and_24_out, instruction_reg1[0], not_26_out);
  and and_25 (and_25_out, not_27_out, not_28_out);
  D_Flip_Flop #(.trigger("falling")) d_ff_10 (
    .D(transistor_152_out), .clk(and_15_out), .Q(fg[0]), .reset(reset));  // open: Qn, preset
  and and_26 (and_26_out, and_18_out, and_19_out);
  and and_27 (and_27_out, and_20_out, and_21_out);
  and and_28 (and_28_out, and_22_out, and_23_out);
  and and_29 (and_29_out, and_24_out, and_25_out);
  Pull_Resistor pull_resistor_70 (.node(transistor_113_out[0]));
  Pull_Resistor pull_resistor_71 (.node(transistor_113_out[1]));
  Pull_Resistor pull_resistor_72 (.node(transistor_113_out[2]));
  Pull_Resistor pull_resistor_73 (.node(transistor_113_out[3]));
  Pull_Resistor pull_resistor_74 (.node(transistor_113_out[4]));
  Pull_Resistor pull_resistor_75 (.node(transistor_113_out[5]));
  Pull_Resistor pull_resistor_76 (.node(transistor_113_out[6]));
  Pull_Resistor pull_resistor_77 (.node(transistor_113_out[7]));
  or or_10 (or_10_out, ALU_ADD, ALU_SUB, ALU_NAND, ALU_NOR);
  Transistor transistor_137 (.in(nor_1_out), .out(transistor_113_out[0]), .gate(not_29_out));
  nor nor_1 (nor_1_out, register_7_q[0], register_6_q[0]);
  Transistor transistor_138 (.in(nor_2_out), .out(transistor_113_out[1]), .gate(not_29_out));
  nor nor_2 (nor_2_out, register_7_q[1], register_6_q[1]);
  Transistor transistor_139 (.in(nor_3_out), .out(transistor_113_out[2]), .gate(not_29_out));
  nor nor_3 (nor_3_out, register_7_q[2], register_6_q[2]);
  Transistor transistor_140 (.in(nor_4_out), .out(transistor_113_out[3]), .gate(not_29_out));
  nor nor_4 (nor_4_out, register_7_q[3], register_6_q[3]);
  Transistor transistor_141 (.in(nor_5_out), .out(transistor_113_out[4]), .gate(not_29_out));
  nor nor_5 (nor_5_out, register_7_q[4], register_6_q[4]);
  Transistor transistor_142 (.in(nor_6_out), .out(transistor_113_out[5]), .gate(not_29_out));
  nor nor_6 (nor_6_out, register_7_q[5], register_6_q[5]);
  Transistor transistor_143 (.in(nor_7_out), .out(transistor_113_out[6]), .gate(not_29_out));
  nor nor_7 (nor_7_out, register_7_q[6], register_6_q[6]);
  Transistor transistor_144 (.in(nor_8_out), .out(transistor_113_out[7]), .gate(not_29_out));
  nor nor_8 (nor_8_out, register_7_q[7], register_6_q[7]);
  not not_29 (not_29_out, ALU_NOR);
  Register register_8 (.D(transistor_113_out), .en(or_10_out), .clk(clk), .Q(register_8_q), .clr(reset));
  Pull_Resistor pull_resistor_78 (.node(pull_resistor_78_node[0]));
  Pull_Resistor pull_resistor_79 (.node(pull_resistor_78_node[1]));
  Pull_Resistor pull_resistor_80 (.node(pull_resistor_78_node[2]));
  Pull_Resistor pull_resistor_81 (.node(pull_resistor_78_node[3]));
  Pull_Resistor pull_resistor_82 (.node(pull_resistor_78_node[4]));
  Pull_Resistor pull_resistor_83 (.node(pull_resistor_78_node[5]));
  Pull_Resistor pull_resistor_84 (.node(pull_resistor_78_node[6]));
  Pull_Resistor pull_resistor_85 (.node(pull_resistor_78_node[7]));
  Pull_Resistor pull_resistor_86 (.node(pull_resistor_86_node[0]));
  Pull_Resistor pull_resistor_87 (.node(pull_resistor_86_node[1]));
  Pull_Resistor pull_resistor_88 (.node(pull_resistor_86_node[2]));
  Pull_Resistor pull_resistor_89 (.node(pull_resistor_86_node[3]));
  Pull_Resistor pull_resistor_90 (.node(pull_resistor_86_node[4]));
  Pull_Resistor pull_resistor_91 (.node(pull_resistor_86_node[5]));
  Pull_Resistor pull_resistor_92 (.node(pull_resistor_86_node[6]));
  Pull_Resistor pull_resistor_93 (.node(pull_resistor_86_node[7]));
  Transistor transistor_145 (.in(1'b1), .out(transistor_145_out), .gate(register_6_q[0]));
  Transistor transistor_146 (.in(transistor_145_out), .out(transistor_146_out), .gate(register_6_q[1]));
  Transistor transistor_147 (.in(transistor_146_out), .out(transistor_147_out), .gate(register_6_q[2]));
  Transistor transistor_148 (.in(transistor_147_out), .out(transistor_148_out), .gate(register_6_q[3]));
  Transistor transistor_149 (.in(transistor_148_out), .out(transistor_149_out), .gate(register_6_q[4]));
  Transistor transistor_150 (.in(transistor_149_out), .out(transistor_150_out), .gate(register_6_q[5]));
  Transistor transistor_151 (.in(transistor_150_out), .out(transistor_151_out), .gate(register_6_q[6]));
  Transistor transistor_152 (.in(transistor_151_out), .out(transistor_152_out), .gate(register_6_q[7]));
  Pull_Resistor pull_resistor_94 (.node(transistor_152_out));
  Transistor transistor_153 (.in(address_bus[0]), .out(pull_resistor_78_node[0]), .gate(not_30_out));
  Transistor transistor_154 (.in(address_bus[1]), .out(pull_resistor_78_node[1]), .gate(not_30_out));
  Transistor transistor_155 (.in(address_bus[2]), .out(pull_resistor_78_node[2]), .gate(not_30_out));
  Transistor transistor_156 (.in(address_bus[3]), .out(pull_resistor_78_node[3]), .gate(not_30_out));
  Transistor transistor_157 (.in(address_bus[4]), .out(pull_resistor_78_node[4]), .gate(not_30_out));
  Transistor transistor_158 (.in(address_bus[5]), .out(pull_resistor_78_node[5]), .gate(not_30_out));
  Transistor transistor_159 (.in(address_bus[6]), .out(pull_resistor_78_node[6]), .gate(not_30_out));
  Transistor transistor_160 (.in(address_bus[7]), .out(pull_resistor_78_node[7]), .gate(not_30_out));
  Transistor transistor_161 (.in(address_bus[8]), .out(pull_resistor_86_node[0]), .gate(not_30_out));
  Transistor transistor_162 (.in(address_bus[9]), .out(pull_resistor_86_node[1]), .gate(not_30_out));
  Transistor transistor_163 (.in(address_bus[10]), .out(pull_resistor_86_node[2]), .gate(not_30_out));
  Transistor transistor_164 (.in(address_bus[11]), .out(pull_resistor_86_node[3]), .gate(not_30_out));
  Transistor transistor_165 (.in(address_bus[12]), .out(pull_resistor_86_node[4]), .gate(not_30_out));
  Transistor transistor_166 (.in(address_bus[13]), .out(pull_resistor_86_node[5]), .gate(not_30_out));
  Transistor transistor_167 (.in(address_bus[14]), .out(pull_resistor_86_node[6]), .gate(not_30_out));
  Transistor transistor_168 (.in(address_bus[15]), .out(pull_resistor_86_node[7]), .gate(not_30_out));
  not not_30 (not_30_out, SAVE_ADDR_A);
  and and_30 (and_30_out, SAVE_DB_IR0, and_26_out);
  and and_31 (and_31_out, SAVE_DB_IR1, and_27_out);
  and and_32 (and_32_out, SAVE_DB_IR0, and_28_out);
  or or_11 (or_11_out, and_32_out, SAVE_ADDR_A, and_33_out);
  and and_33 (and_33_out, SAVE_DB_IR1, and_29_out);
  Transistor transistor_169 (.in(register_8_q[0]), .out(data_bus[0]), .gate(not_31_out));
  Transistor transistor_170 (.in(register_8_q[1]), .out(data_bus[1]), .gate(not_31_out));
  Transistor transistor_171 (.in(register_8_q[2]), .out(data_bus[2]), .gate(not_31_out));
  Transistor transistor_172 (.in(register_8_q[3]), .out(data_bus[3]), .gate(not_31_out));
  Transistor transistor_173 (.in(register_8_q[4]), .out(data_bus[4]), .gate(not_31_out));
  Transistor transistor_174 (.in(register_8_q[5]), .out(data_bus[5]), .gate(not_31_out));
  Transistor transistor_175 (.in(register_8_q[6]), .out(data_bus[6]), .gate(not_31_out));
  Transistor transistor_176 (.in(register_8_q[7]), .out(data_bus[7]), .gate(not_31_out));
  not not_31 (not_31_out, PUT_ALUOUT_DB);
  or or_12 (or_12_out, and_30_out, SAVE_ADDR_A, and_31_out);
  xor xor_6 (xor_6_out, register_6_q[0], register_7_q[0]);
  xor xor_7 (xor_7_out, register_6_q[1], register_7_q[1]);
  xor xor_8 (xor_8_out, register_6_q[2], register_7_q[2]);
  xor xor_9 (xor_9_out, register_6_q[3], register_7_q[3]);
  xor xor_10 (xor_10_out, register_6_q[4], register_7_q[4]);
  xor xor_11 (xor_11_out, register_6_q[5], register_7_q[5]);
  xor xor_12 (xor_12_out, register_6_q[6], register_7_q[6]);
  xor xor_13 (xor_13_out, register_6_q[7], register_7_q[7]);
  assign or_13_out = pull_resistor_78_node | data_bus;  // OR_Gate or_13, 8 bits wide
  assign or_14_out = pull_resistor_86_node | data_bus;  // OR_Gate or_14, 8 bits wide
  Register #(.trigger("falling")) register_9 (.D(or_13_out), .en(or_12_out), .clk(clk), .Q(register_9_q), .clr(reset));
  and and_34 (and_34_out, PUT_IR0_DB, and_26_out);
  and and_35 (and_35_out, PUT_IR1_DB, and_27_out);
  Register #(.trigger("falling")) register_10 (
    .D(or_14_out), .en(or_11_out), .clk(clk), .Q(register_10_q), .clr(reset));
  and and_36 (and_36_out, PUT_IR0_DB, and_28_out);
  and and_37 (and_37_out, PUT_IR1_DB, and_29_out);
  Transistor transistor_177 (.in(1'b1), .out(transistor_177_out), .gate(xor_6_out));
  Transistor transistor_178 (.in(transistor_177_out), .out(transistor_178_out), .gate(xor_7_out));
  Transistor transistor_179 (.in(transistor_178_out), .out(transistor_179_out), .gate(xor_8_out));
  Transistor transistor_180 (.in(transistor_179_out), .out(transistor_180_out), .gate(xor_9_out));
  Transistor transistor_181 (.in(transistor_180_out), .out(transistor_181_out), .gate(xor_10_out));
  Transistor transistor_182 (.in(transistor_181_out), .out(transistor_182_out), .gate(xor_11_out));
  Transistor transistor_183 (.in(transistor_182_out), .out(transistor_183_out), .gate(xor_12_out));
  Transistor transistor_184 (.in(transistor_183_out), .out(transistor_184_out), .gate(xor_13_out));
  Pull_Resistor pull_resistor_95 (.node(transistor_184_out));
  or or_15 (or_15_out, and_34_out, and_35_out);
  or or_16 (or_16_out, and_36_out, and_37_out);
  Transistor transistor_185 (.in(register_9_q[0]), .out(data_bus[0]), .gate(not_32_out));
  Transistor transistor_186 (.in(register_9_q[1]), .out(data_bus[1]), .gate(not_32_out));
  Transistor transistor_187 (.in(register_9_q[2]), .out(data_bus[2]), .gate(not_32_out));
  Transistor transistor_188 (.in(register_9_q[3]), .out(data_bus[3]), .gate(not_32_out));
  Transistor transistor_189 (.in(register_9_q[4]), .out(data_bus[4]), .gate(not_32_out));
  Transistor transistor_190 (.in(register_9_q[5]), .out(data_bus[5]), .gate(not_32_out));
  Transistor transistor_191 (.in(register_9_q[6]), .out(data_bus[6]), .gate(not_32_out));
  Transistor transistor_192 (.in(register_9_q[7]), .out(data_bus[7]), .gate(not_32_out));
  not not_32 (not_32_out, or_15_out);
  Transistor transistor_193 (.in(register_10_q[0]), .out(data_bus[0]), .gate(not_33_out));
  Transistor transistor_194 (.in(register_10_q[1]), .out(data_bus[1]), .gate(not_33_out));
  Transistor transistor_195 (.in(register_10_q[2]), .out(data_bus[2]), .gate(not_33_out));
  Transistor transistor_196 (.in(register_10_q[3]), .out(data_bus[3]), .gate(not_33_out));
  Transistor transistor_197 (.in(register_10_q[4]), .out(data_bus[4]), .gate(not_33_out));
  Transistor transistor_198 (.in(register_10_q[5]), .out(data_bus[5]), .gate(not_33_out));
  Transistor transistor_199 (.in(register_10_q[6]), .out(data_bus[6]), .gate(not_33_out));
  Transistor transistor_200 (.in(register_10_q[7]), .out(data_bus[7]), .gate(not_33_out));
  not not_33 (not_33_out, or_16_out);
  not not_34 (not_34_out, PUT_A_ADDR);
  Transistor transistor_201 (.in(register_9_q[0]), .out(address_bus[0]), .gate(not_34_out));
  Transistor transistor_202 (.in(register_9_q[1]), .out(address_bus[1]), .gate(not_34_out));
  Transistor transistor_203 (.in(register_9_q[2]), .out(address_bus[2]), .gate(not_34_out));
  Transistor transistor_204 (.in(register_9_q[3]), .out(address_bus[3]), .gate(not_34_out));
  Transistor transistor_205 (.in(register_9_q[4]), .out(address_bus[4]), .gate(not_34_out));
  Transistor transistor_206 (.in(register_9_q[5]), .out(address_bus[5]), .gate(not_34_out));
  Transistor transistor_207 (.in(register_9_q[6]), .out(address_bus[6]), .gate(not_34_out));
  Transistor transistor_208 (.in(register_9_q[7]), .out(address_bus[7]), .gate(not_34_out));
  Transistor transistor_209 (.in(register_10_q[0]), .out(address_bus[8]), .gate(not_34_out));
  Transistor transistor_210 (.in(register_10_q[1]), .out(address_bus[9]), .gate(not_34_out));
  Transistor transistor_211 (.in(register_10_q[2]), .out(address_bus[10]), .gate(not_34_out));
  Transistor transistor_212 (.in(register_10_q[3]), .out(address_bus[11]), .gate(not_34_out));
  Transistor transistor_213 (.in(register_10_q[4]), .out(address_bus[12]), .gate(not_34_out));
  Transistor transistor_214 (.in(register_10_q[5]), .out(address_bus[13]), .gate(not_34_out));
  Transistor transistor_215 (.in(register_10_q[6]), .out(address_bus[14]), .gate(not_34_out));
  Transistor transistor_216 (.in(register_10_q[7]), .out(address_bus[15]), .gate(not_34_out));
  not not_35 (not_35_out, instruction_reg0[0]);
  not not_36 (not_36_out, instruction_reg0[1]);
  not not_37 (not_37_out, instruction_reg0[3]);
  not not_38 (not_38_out, instruction_reg1[0]);
  not not_39 (not_39_out, instruction_reg1[1]);
  not not_40 (not_40_out, instruction_reg1[3]);
  not not_41 (not_41_out, instruction_reg0[1]);
  not not_42 (not_42_out, instruction_reg0[3]);
  not not_43 (not_43_out, instruction_reg1[1]);
  not not_44 (not_44_out, instruction_reg1[3]);
  not not_45 (not_45_out, instruction_reg0[0]);
  not not_46 (not_46_out, instruction_reg0[2]);
  not not_47 (not_47_out, instruction_reg0[3]);
  not not_48 (not_48_out, instruction_reg1[0]);
  not not_49 (not_49_out, instruction_reg1[2]);
  not not_50 (not_50_out, instruction_reg1[3]);
  and and_38 (and_38_out, instruction_reg0[0], instruction_reg0[1]);
  not not_51 (not_51_out, instruction_reg0[2]);
  and and_39 (and_39_out, not_51_out, not_52_out);
  not not_52 (not_52_out, instruction_reg0[3]);
  and and_40 (and_40_out, instruction_reg1[0], instruction_reg1[1]);
  not not_53 (not_53_out, instruction_reg1[2]);
  and and_41 (and_41_out, not_53_out, not_54_out);
  not not_54 (not_54_out, instruction_reg1[3]);
  and and_42 (and_42_out, not_35_out, not_36_out);
  and and_43 (and_43_out, instruction_reg0[2], not_37_out);
  and and_44 (and_44_out, not_38_out, not_39_out);
  and and_45 (and_45_out, instruction_reg1[2], not_40_out);
  and and_46 (and_46_out, instruction_reg0[0], not_41_out);
  and and_47 (and_47_out, instruction_reg0[2], not_42_out);
  and and_48 (and_48_out, instruction_reg1[0], not_43_out);
  and and_49 (and_49_out, instruction_reg1[2], not_44_out);
  and and_50 (and_50_out, not_45_out, instruction_reg0[1]);
  and and_51 (and_51_out, not_46_out, not_47_out);
  and and_52 (and_52_out, not_48_out, instruction_reg1[1]);
  and and_53 (and_53_out, not_49_out, not_50_out);
  and and_54 (and_54_out, and_38_out, and_39_out);
  and and_55 (and_55_out, and_40_out, and_41_out);
  and and_56 (and_56_out, and_42_out, and_43_out);
  and and_57 (and_57_out, and_44_out, and_45_out);
  and and_58 (and_58_out, and_46_out, and_47_out);
  and and_59 (and_59_out, and_48_out, and_49_out);
  and and_60 (and_60_out, and_50_out, and_51_out);
  and and_61 (and_61_out, and_52_out, and_53_out);
  Pull_Resistor pull_resistor_96 (.node(pull_resistor_96_node[0]));
  Pull_Resistor pull_resistor_97 (.node(pull_resistor_96_node[1]));
  Pull_Resistor pull_resistor_98 (.node(pull_resistor_96_node[2]));
  Pull_Resistor pull_resistor_99 (.node(pull_resistor_96_node[3]));
  Pull_Resistor pull_resistor_100 (.node(pull_resistor_96_node[4]));
  Pull_Resistor pull_resistor_101 (.node(pull_resistor_96_node[5]));
  Pull_Resistor pull_resistor_102 (.node(pull_resistor_96_node[6]));
  Pull_Resistor pull_resistor_103 (.node(pull_resistor_96_node[7]));
  Pull_Resistor pull_resistor_104 (.node(pull_resistor_104_node[0]));
  Pull_Resistor pull_resistor_105 (.node(pull_resistor_104_node[1]));
  Pull_Resistor pull_resistor_106 (.node(pull_resistor_104_node[2]));
  Pull_Resistor pull_resistor_107 (.node(pull_resistor_104_node[3]));
  Pull_Resistor pull_resistor_108 (.node(pull_resistor_104_node[4]));
  Pull_Resistor pull_resistor_109 (.node(pull_resistor_104_node[5]));
  Pull_Resistor pull_resistor_110 (.node(pull_resistor_104_node[6]));
  Pull_Resistor pull_resistor_111 (.node(pull_resistor_104_node[7]));
  not not_55 (not_55_out, SAVE_ADDR_B);
  and and_62 (and_62_out, SAVE_DB_IR0, and_54_out);
  and and_63 (and_63_out, SAVE_DB_IR1, and_55_out);
  and and_64 (and_64_out, SAVE_DB_IR0, and_56_out);
  and and_65 (and_65_out, SAVE_DB_IR1, and_57_out);
  and and_66 (and_66_out, SAVE_DB_IR0, and_58_out);
  and and_67 (and_67_out, SAVE_DB_IR1, and_59_out);
  Transistor transistor_217 (.in(address_bus[0]), .out(pull_resistor_96_node[0]), .gate(not_55_out));
  Transistor transistor_218 (.in(address_bus[1]), .out(pull_resistor_96_node[1]), .gate(not_55_out));
  Transistor transistor_219 (.in(address_bus[2]), .out(pull_resistor_96_node[2]), .gate(not_55_out));
  Transistor transistor_220 (.in(address_bus[3]), .out(pull_resistor_96_node[3]), .gate(not_55_out));
  Transistor transistor_221 (.in(address_bus[4]), .out(pull_resistor_96_node[4]), .gate(not_55_out));
  Transistor transistor_222 (.in(address_bus[5]), .out(pull_resistor_96_node[5]), .gate(not_55_out));
  Transistor transistor_223 (.in(address_bus[6]), .out(pull_resistor_96_node[6]), .gate(not_55_out));
  Transistor transistor_224 (.in(address_bus[7]), .out(pull_resistor_96_node[7]), .gate(not_55_out));
  Transistor transistor_225 (.in(address_bus[8]), .out(pull_resistor_104_node[0]), .gate(not_55_out));
  Transistor transistor_226 (.in(address_bus[9]), .out(pull_resistor_104_node[1]), .gate(not_55_out));
  Transistor transistor_227 (.in(address_bus[10]), .out(pull_resistor_104_node[2]), .gate(not_55_out));
  Transistor transistor_228 (.in(address_bus[11]), .out(pull_resistor_104_node[3]), .gate(not_55_out));
  Transistor transistor_229 (.in(address_bus[12]), .out(pull_resistor_104_node[4]), .gate(not_55_out));
  Transistor transistor_230 (.in(address_bus[13]), .out(pull_resistor_104_node[5]), .gate(not_55_out));
  Transistor transistor_231 (.in(address_bus[14]), .out(pull_resistor_104_node[6]), .gate(not_55_out));
  Transistor transistor_232 (.in(address_bus[15]), .out(pull_resistor_104_node[7]), .gate(not_55_out));
  and and_68 (and_68_out, SAVE_DB_IR0, and_60_out);
  or or_17 (or_17_out, and_68_out, SAVE_ADDR_B, and_69_out);
  and and_69 (and_69_out, SAVE_DB_IR1, and_61_out);
  or or_18 (or_18_out, and_62_out, SAVE_ADDR_B, and_63_out);
  or or_19 (or_19_out, and_64_out, and_65_out);
  or or_20 (or_20_out, and_66_out, and_67_out);
  Register #(.trigger("falling")) register_11 (
    .D(or_22_out), .en(or_18_out), .clk(clk), .Q(register_11_q), .clr(reset));
  Register #(.trigger("falling")) register_12 (.D(data_bus), .en(or_19_out), .clk(clk), .Q(register_12_q), .clr(reset));
  and and_70 (and_70_out, PUT_IR0_DB, and_56_out);
  and and_71 (and_71_out, PUT_IR1_DB, and_57_out);
  Register #(.trigger("falling")) register_13 (.D(data_bus), .en(or_20_out), .clk(clk), .Q(register_13_q), .clr(reset));
  and and_72 (and_72_out, PUT_IR0_DB, and_58_out);
  and and_73 (and_73_out, PUT_IR1_DB, and_59_out);
  assign or_21_out = pull_resistor_96_node | data_bus;  // OR_Gate or_21, 8 bits wide
  assign or_22_out = pull_resistor_104_node | data_bus;  // OR_Gate or_22, 8 bits wide
  Register #(.trigger("falling")) register_14 (
    .D(or_21_out), .en(or_17_out), .clk(clk), .Q(register_14_q), .clr(reset));
  and and_74 (and_74_out, PUT_IR0_DB, and_60_out);
  and and_75 (and_75_out, PUT_IR1_DB, and_61_out);
  and and_76 (and_76_out, PUT_IR0_DB, and_54_out);
  and and_77 (and_77_out, PUT_IR1_DB, and_55_out);
  or or_23 (or_23_out, and_74_out, and_75_out);
  or or_24 (or_24_out, and_76_out, and_77_out);
  not not_56 (not_56_out, or_24_out);
  or or_25 (or_25_out, and_70_out, and_71_out);
  not not_57 (not_57_out, or_25_out);
  or or_26 (or_26_out, and_72_out, and_73_out);
  not not_58 (not_58_out, or_26_out);
  Transistor transistor_233 (.in(register_14_q[0]), .out(data_bus[0]), .gate(not_59_out));
  Transistor transistor_234 (.in(register_14_q[1]), .out(data_bus[1]), .gate(not_59_out));
  Transistor transistor_235 (.in(register_14_q[2]), .out(data_bus[2]), .gate(not_59_out));
  Transistor transistor_236 (.in(register_14_q[3]), .out(data_bus[3]), .gate(not_59_out));
  Transistor transistor_237 (.in(register_14_q[4]), .out(data_bus[4]), .gate(not_59_out));
  Transistor transistor_238 (.in(register_14_q[5]), .out(data_bus[5]), .gate(not_59_out));
  Transistor transistor_239 (.in(register_14_q[6]), .out(data_bus[6]), .gate(not_59_out));
  Transistor transistor_240 (.in(register_14_q[7]), .out(data_bus[7]), .gate(not_59_out));
  not not_59 (not_59_out, or_23_out);
  Transistor transistor_241 (.in(register_11_q[0]), .out(data_bus[0]), .gate(not_56_out));
  Transistor transistor_242 (.in(register_11_q[1]), .out(data_bus[1]), .gate(not_56_out));
  Transistor transistor_243 (.in(register_11_q[2]), .out(data_bus[2]), .gate(not_56_out));
  Transistor transistor_244 (.in(register_11_q[3]), .out(data_bus[3]), .gate(not_56_out));
  Transistor transistor_245 (.in(register_11_q[4]), .out(data_bus[4]), .gate(not_56_out));
  Transistor transistor_246 (.in(register_11_q[5]), .out(data_bus[5]), .gate(not_56_out));
  Transistor transistor_247 (.in(register_11_q[6]), .out(data_bus[6]), .gate(not_56_out));
  Transistor transistor_248 (.in(register_11_q[7]), .out(data_bus[7]), .gate(not_56_out));
  Transistor transistor_249 (.in(register_12_q[0]), .out(data_bus[0]), .gate(not_57_out));
  Transistor transistor_250 (.in(register_12_q[1]), .out(data_bus[1]), .gate(not_57_out));
  Transistor transistor_251 (.in(register_12_q[2]), .out(data_bus[2]), .gate(not_57_out));
  Transistor transistor_252 (.in(register_12_q[3]), .out(data_bus[3]), .gate(not_57_out));
  Transistor transistor_253 (.in(register_12_q[4]), .out(data_bus[4]), .gate(not_57_out));
  Transistor transistor_254 (.in(register_12_q[5]), .out(data_bus[5]), .gate(not_57_out));
  Transistor transistor_255 (.in(register_12_q[6]), .out(data_bus[6]), .gate(not_57_out));
  Transistor transistor_256 (.in(register_12_q[7]), .out(data_bus[7]), .gate(not_57_out));
  Transistor transistor_257 (.in(register_13_q[0]), .out(data_bus[0]), .gate(not_58_out));
  Transistor transistor_258 (.in(register_13_q[1]), .out(data_bus[1]), .gate(not_58_out));
  Transistor transistor_259 (.in(register_13_q[2]), .out(data_bus[2]), .gate(not_58_out));
  Transistor transistor_260 (.in(register_13_q[3]), .out(data_bus[3]), .gate(not_58_out));
  Transistor transistor_261 (.in(register_13_q[4]), .out(data_bus[4]), .gate(not_58_out));
  Transistor transistor_262 (.in(register_13_q[5]), .out(data_bus[5]), .gate(not_58_out));
  Transistor transistor_263 (.in(register_13_q[6]), .out(data_bus[6]), .gate(not_58_out));
  Transistor transistor_264 (.in(register_13_q[7]), .out(data_bus[7]), .gate(not_58_out));
  not not_60 (not_60_out, PUT_B_ADDR);
  Transistor transistor_265 (.in(register_14_q[0]), .out(address_bus[0]), .gate(not_60_out));
  Transistor transistor_266 (.in(register_14_q[1]), .out(address_bus[1]), .gate(not_60_out));
  Transistor transistor_267 (.in(register_14_q[2]), .out(address_bus[2]), .gate(not_60_out));
  Transistor transistor_268 (.in(register_14_q[3]), .out(address_bus[3]), .gate(not_60_out));
  Transistor transistor_269 (.in(register_14_q[4]), .out(address_bus[4]), .gate(not_60_out));
  Transistor transistor_270 (.in(register_14_q[5]), .out(address_bus[5]), .gate(not_60_out));
  Transistor transistor_271 (.in(register_14_q[6]), .out(address_bus[6]), .gate(not_60_out));
  Transistor transistor_272 (.in(register_14_q[7]), .out(address_bus[7]), .gate(not_60_out));
  Transistor transistor_273 (.in(register_11_q[0]), .out(address_bus[8]), .gate(not_60_out));
  Transistor transistor_274 (.in(register_11_q[1]), .out(address_bus[9]), .gate(not_60_out));
  Transistor transistor_275 (.in(register_11_q[2]), .out(address_bus[10]), .gate(not_60_out));
  Transistor transistor_276 (.in(register_11_q[3]), .out(address_bus[11]), .gate(not_60_out));
  Transistor transistor_277 (.in(register_11_q[4]), .out(address_bus[12]), .gate(not_60_out));
  Transistor transistor_278 (.in(register_11_q[5]), .out(address_bus[13]), .gate(not_60_out));
  Transistor transistor_279 (.in(register_11_q[6]), .out(address_bus[14]), .gate(not_60_out));
  Transistor transistor_280 (.in(register_11_q[7]), .out(address_bus[15]), .gate(not_60_out));

  // Other names for the same wires on the sheet: PUT_MEM_DB = memory_read; SAVE_DB_MEM = memory_write

  // Notes on the sheet:
  //   contents of rom_1 (hex, n*v repeats v):
  //   2 0 0 2 1 1 2 2 b 1 3 0 6 13 0 1 10 0 1 31 0 9 2 1 f 2 0 21 9 0 22 0 0 3 3 0 2 4 0 3 4 0 1d 1e 0 1d
  //   ff ff
  //   contents of rom_2 (hex, n*v repeats v):
  //   0 80000000 7*0 c 80000000 6*0 28 80000000 6*0 800003 80000000 6*0 400009 80000000 6*0 1801 40000
  //   80000000 5*0 42 84 100 408 80000000 0 0 0 42 a0 100 408 80000000 0 0 0 42 84 80000 408 80000000 0 0
  //   0 42 a0 80000 408 80000000 0 0 0 42 84 100000 408 80000000 0 0 0 42 a0 80000 408 80000000 0 0 0 42
  //   84 200000 408 80000000 0 0 0 42 a0 200000 408 80000000 0 0 0 42 84 200 80000000 4*0 42 a0 200
  //   80000000 4*0 1001 40000 80000000 5*0 10009 80000000 6*0 8003 80000000 6*0 4001 20000 0 80000000 4*0
  //   2001 40000 80000000 5*0 2801 40000 80000000 5*0 1001800 40000 80000000 5*0 1001000 40000 80000000
  //   5*0 1004000 20000 0 80000000 4*0 1002000 40000 80000000 5*0 1002800 40000 80000000 5*0 1010008
  //   80000000 6*0 1008002 80000000 6*0 2004000 20000 0 80000000 4*0 2002000 40000 80000000 5*0 2002800
  //   40000 80000000 13*0 2001800 40000 80000000 5*0 6000000 80000000 6*0 a000000 80000000
  //   buffer_1 drives only 1 and floats otherwise
  //   buffer_2 drives only 1 and floats otherwise
  //   buffer_3 drives only 1 and floats otherwise
  //   buffer_4 drives only 1 and floats otherwise
  //   buffer_5 drives only 1 and floats otherwise
  //   buffer_6 drives only 1 and floats otherwise
  //   buffer_7 drives only 1 and floats otherwise
endmodule
